# Fritzing sketch Vibration_motor_Automatic_BT_TOTAL (saved by Fritzing 0.8.7b)
breadboards: 1

parts:
  Componente1 = Arduino Uno (Rev3)
  SW-1 = Vibration sensor module
  Componente2 = Bluetooth HC-05 Macho
  S1 = Pushbutton [package="[THT]"]
  Componente3 = SRF05 Ultrasonic Rangefinder
  R1 = Resistor [package="2512 [SMD]"]
  VCC1 = Battery block 9V

nets:
  N1: Componente1.D8, SW-1.Digital_output
  N2: Componente1.D9_PWM, Componente3.Echo
  N3: Componente1.D10_PWM/SS, Componente3.Trig
  GND: Componente1.GND, Componente1.D7, SW-1.Ground, Componente2.GND, S1.Pin_1, S1.Pin_2, Componente3.GND, VCC1.-
  N4: Componente1.D0/RX, Componente2.TXD
  N5: Componente1.D1/TX, Componente2.RXD
  VCC: Componente1.5V, SW-1.vcc, Componente2.VCC, S1.Pin_3, S1.Pin_4, Componente3.VCC, R1.Pin_0
  N6: Componente1.VIN, VCC1.+

custom parts:
  Vibration sensor module: Single-roller type full induction trigger switch. When no vibration or tilt, the product is ON conduction state, and in the steady state, when a vibration or tilt, the switch will be rendered instantly disconnect the conductive resistance increases, generating a current pulse signal, thereby triggering circuit. The default state of the swith is close Digital output Supply voltage:3.3V-5V On-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
