# Fritzing sketch Vibration_motor_Manual_BT (saved by Fritzing 0.8.7b)
breadboards: 1

parts:
  Componente1 = Arduino Uno (Rev3)
  SW-1 = Vibration sensor module
  Componente2 = Bluetooth HC-05 Macho
  Componente3 = SRF05 Ultrasonic Rangefinder

nets:
  N1: Componente1.D8, SW-1.Digital_output
  N2: Componente1.D9_PWM, Componente3.Echo
  N3: Componente1.D10_PWM/SS, Componente3.Trig
  N4: Componente1.D0/RX, Componente2.TXD
  N5: Componente1.D1/TX, Componente2.RXD
  VCC: Componente1.5V, SW-1.vcc, Componente2.VCC, Componente3.VCC
  GND: Componente1.GND, SW-1.Ground, Componente2.GND, Componente3.GND

custom parts:
  Vibration sensor module: Single-roller type full induction trigger switch. When no vibration or tilt, the product is ON conduction state, and in the steady state, when a vibration or tilt, the switch will be rendered instantly disconnect the conductive resistance increases, generating a current pulse signal, thereby triggering circuit. The default state of the swith is close Digital output Supply voltage:3.3V-5V On-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
